# Fritzing sketch work in progress planty fritzing will finish in class. (saved by Fritzing 1.0.2b)
breadboards: 1

parts:
  Grove1 = Grove Dust Sensor
  A1 = Particle - Photon2
  OLED_I2C1 = OLED 128x64 I2C Monochrome Display
  M1 = BMP280
  Part1 = MQ-131 breakout
  Relay1 = Relay - 6 pins [package="DIP (Dual Inline) [THT]"]  # not connected

nets:
  GND: Grove1.GND, OLED_I2C1.GND, M1.GND, Part1.GND
  N1: Grove1.SIG, A1.Pin_15
  N2: A1.Pin_17, OLED_I2C1.SDA, M1.SDA
  N3: A1.Pin_18, OLED_I2C1.SCK, M1.SCL
  VDD: OLED_I2C1.VDD, M1.VIN, Part1.VCC

custom parts:
  Grove Dust Sensor: PPD42 Grove Dust Sensor
  Particle - Photon2: The Photon 2 is a microcontroller and Wi-Fi networking developed by particle. Features: 802.11a/b/g/n Wi-Fi, 2.4 GHz and 5 GHz Integrated PCB antenna Integrated U.FL connector for external antenna Integrated RF switch BLE 5 using same antenna as Wi-Fi Realtek RTL8721DM MCU ARM Cortex M33 CPU, 200 MHz 2048 KB (2 MB) user application maximum size 3072 KB (3 MB) of RAM available to user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
  BMP280: Temperature Humidity Barometric presure Sensor, I2C
  MQ-131 breakout: SKU: 101282
  Relay - 6 pins: A DIP stand-in part for whatever IC you want. With 6 pins on a 900mil dual inline package (DIP) footprint.
